// Logisim project project CN262 Fast Arrow.circ as structural Verilog: 11 circuits, main circuit main
module main (
  output [1:0] out_1,
  output [1:0] out_2,
  output [6:0] Keyboard_input
);

  wire check, click, clk, comparator_1_eq, comparator_2_eq, controlled_buffer_1_out, \end , k5,
       keyboard_1_avail, register_1_q, reset, secclk, start, stop, timer_1_out_8;
  wire [11:0] output1, output2;
  wire [31:0] display_1_out_2, display_1_out_3, output3, output4, pass_1_out_2, pass_1_out_3, ready_1_out_3,
       ready_1_out_4, stop_1_out_1, stop_1_out_2;

  Clock clock_1 (.out(clk));
  Register #(.width(1)) register_1 (.D(check), .Q(register_1_q), .clk(clk));  // open: en, clr
  Clock clock_2 (.out(clk));
  Button button_1 (.out(start));
  secclock secclock_1 (.in_1(clk), .in_2(start), .out_3(secclk));
  stage_control stage_control_1 (
    .in_4(\end ), .out_7(out_1), .in_1(start), .in_2(secclk), .in_5(out_1), .in_3(clk), .in_6(check),
    .out_8(reset));
  random random_1 (.out_4(out_2), .in_1(secclk), .in_2(register_1_q), .in_3(out_1));
  Button button_2 (.out(stop));
  check_key check_key_1 (.out_3(click), .out_4(check), .in_1(Keyboard_input), .in_2(out_2));
  assign controlled_buffer_1_out = keyboard_1_avail ? clk : 1'bz;  // Controlled_Buffer controlled_buffer_1
  Keyboard keyboard_1 (
    .clk(controlled_buffer_1_out), .clr(comparator_2_eq), .avail(keyboard_1_avail), .data(Keyboard_input));  // open: re
  display display_1 (.in_1(out_2), .out_2(display_1_out_2), .out_3(display_1_out_3));
  TTY tty_1 (.data(Keyboard_input), .clk(clk), .clr(reset));  // open: we
  DotMatrix #(.matrixcols(8), .matrixrows(8)) dotmatrix_1 (
    .col0(output3[31:24]), .col1(output3[23:16]), .col2(output3[15:8]), .col3(output3[7:0]),
    .col4(output4[31:24]), .col5(output4[23:16]), .col6(output4[15:8]), .col7(output4[7:0]));
  Multiplexer #(.select(2), .width(32)) multiplexer_1 (
    .in0(stop_1_out_1), .in1(ready_1_out_3), .in2(display_1_out_2), .in3(pass_1_out_2), .out(output3),
    .sel(out_1));  // open: en
  Comparator #(.width(7)) comparator_1 (.a(Keyboard_input), .b({7{1'b0}}), .eq(comparator_1_eq));  // open: gt, lt
  not not_1 (k5, comparator_1_eq);
  Comparator #(.width(2)) comparator_2 (.a(2'b11), .b(out_1), .eq(comparator_2_eq));  // open: gt, lt
  DotMatrix #(.matrixcols(8), .matrixrows(8)) dotmatrix_2 (
    .col0(output3[31:24]), .col1(output3[23:16]), .col2(output3[15:8]), .col3(output3[7:0]),
    .col4(output4[31:24]), .col5(output4[23:16]), .col6(output4[15:8]), .col7(output4[7:0]));
  Multiplexer #(.select(2), .width(32)) multiplexer_2 (
    .in0(stop_1_out_2), .in1(ready_1_out_4), .in2(display_1_out_3), .in3(pass_1_out_3), .out(output4),
    .sel(out_1));  // open: en
  stop stop_1 (.out_1(stop_1_out_1), .out_2(stop_1_out_2));
  pass pass_1 (.out_2(pass_1_out_2), .out_3(pass_1_out_3), .in_1(check));
  ready ready_1 (.out_3(ready_1_out_3), .out_4(ready_1_out_4), .in_1(secclk), .in_2(reset));
  Hex_Digit_Display hex_digit_display_1 (.value(output1[7:4]));  // open: dp
  Hex_Digit_Display hex_digit_display_2 (.value(output1[11:8]));  // open: dp
  Hex_Digit_Display hex_digit_display_3 (.value(output2[7:4]));  // open: dp
  Hex_Digit_Display hex_digit_display_4 (.value(output2[11:8]));  // open: dp
  Hex_Digit_Display hex_digit_display_5 (.value(output1[3:0]));  // open: dp
  Hex_Digit_Display hex_digit_display_6 (.value(output2[3:0]));  // open: dp
  Hex_Digit_Display hex_digit_display_7 (.value(output1[11:8]));  // open: dp
  Hex_Digit_Display hex_digit_display_8 (.value(output2[11:8]));  // open: dp
  Hex_Digit_Display hex_digit_display_9 (.value(output2[7:4]));  // open: dp
  Hex_Digit_Display hex_digit_display_10 (.value(output1[3:0]));  // open: dp
  Hex_Digit_Display hex_digit_display_11 (.value(output1[7:4]));  // open: dp
  score score_1 (
    .in_1(reset), .in_2(clk), .in_3(check), .out_6(output1[11:8]), .out_7(output1[7:4]),
    .out_8(output1[3:0]), .in_4(click), .in_5(out_1));
  Hex_Digit_Display hex_digit_display_12 (.value(output2[3:0]));  // open: dp
  timer timer_1 (
    .in_3(out_1), .in_4(8'h3c), .out_8(timer_1_out_8), .out_5(output2[11:8]), .out_6(output2[7:4]),
    .out_7(output2[3:0]), .in_2(secclk), .in_1(reset));
  or or_1 (\end , stop, timer_1_out_8);

  // Other names for the same wires on the sheet: k4[6:0] = Keyboard_input; stage[1:0] = out_1

  // Notes on the sheet:
  //   Fast Arrow game
  //   Keyboard
  //   a = left
  //   w = up
  //   *****************************************************************************************************************************************************************************************************************************************************************************************
  //   Score counter
  //   Timer(second) 
  //   s = down
  //   32 Hz 
  //   d = right
  //   1.นายสุเมต              คงแก้ว             6210612559
  //   2.นางสาวอนุรดี     บรรดาศักดิ์     6210612625     
  //   3.นายพรชัย             พุ่มภิญโญ      6210612732
  //   1. Set tick frequnecy to 32 HZ
  //   2. Press start button
  //   3. Game Started!!!!
  //   ลูกศรขึ้น = กดปุ่ม w
  //   ลูกศรลง = กดปุ่ม s
  //   -> กดถูกจะได้ 1 แต้ม
  //   -> กดผิดจะเสีย 1 แต้ม
  //   2. เวลามีทั้งหมด 60 วินาที
  //   Members
  //   วิธีการเล่น
  //   Rules
  //   1.กดปุ่มให้ตรงกับลูกศรที่แสดงบนหน้าจอ
  //   ลูกศรซ้าย = กดปุ่ม a
  //   ลูกศรขวา = กดปุ่ม d
endmodule

module display (
  input  [1:0] in_1,
  output [31:0] out_2,
  output [31:0] out_3
);

  Multiplexer #(.select(2), .width(8)) multiplexer_1 (
    .in0(8'h8), .in1({8{1'b0}}), .in2(8'h10), .in3({8{1'b0}}), .out(out_2[31:24]), .sel(in_1));  // open: en
  Multiplexer #(.select(2), .width(8)) multiplexer_2 (
    .in0(8'h18), .in1(8'h3c), .in2(8'h18), .in3(8'h18), .out(out_2[23:16]), .sel(in_1));  // open: en
  Multiplexer #(.select(2), .width(8)) multiplexer_3 (
    .in0(8'h3e), .in1(8'h3c), .in2(8'h7c), .in3(8'h3c), .out(out_2[15:8]), .sel(in_1));  // open: en
  Multiplexer #(.select(2), .width(8)) multiplexer_4 (
    .in0(8'h7e), .in1({8{1'b1}}), .in2(8'h7e), .in3(8'h7e), .out(out_2[7:0]), .sel(in_1));  // open: en
  Multiplexer #(.select(2), .width(8)) multiplexer_5 (
    .in0(8'h7e), .in1(8'h7e), .in2(8'h7e), .in3({8{1'b1}}), .out(out_3[31:24]), .sel(in_1));  // open: en
  Multiplexer #(.select(2), .width(8)) multiplexer_6 (
    .in0(8'h3e), .in1(8'h3c), .in2(8'h7c), .in3(8'h3c), .out(out_3[23:16]), .sel(in_1));  // open: en
  Multiplexer #(.select(2), .width(8)) multiplexer_7 (
    .in0(8'h18), .in1(8'h18), .in2(8'h18), .in3(8'h3c), .out(out_3[15:8]), .sel(in_1));  // open: en
  Multiplexer #(.select(2), .width(8)) multiplexer_8 (
    .in0(8'h8), .in1({8{1'b0}}), .in2(8'h10), .in3({8{1'b0}}), .out(out_3[7:0]), .sel(in_1));  // open: en

  // Other names for the same wires on the sheet: rd_select[1:0] = in_1
endmodule

module random (
  input  in_1,
  input  in_2,
  input  [1:0] in_3,
  output [1:0] out_4
);

  wire comparator_1_eq, comparator_2_eq, or_1_out;
  wire [1:0] adder_1_out, tt;

  Comparator #(.width(2)) comparator_1 (.a(2'b11), .b(tt), .eq(comparator_1_eq));  // open: gt, lt
  or or_1 (or_1_out, in_2, comparator_1_eq);
  Random #(.width(2)) random_1 (.clk(or_1_out), .out(out_4));  // open: next, clr
  Adder #(.width(2)) adder_1 (.a(tt), .b(2'b01), .out(adder_1_out));  // open: cin, cout
  Register #(.width(2)) register_1 (.D(adder_1_out), .Q(tt), .clk(in_1), .clr(comparator_2_eq));  // open: en
  Comparator #(.width(2)) comparator_2 (.a(2'b10), .b(in_3), .eq(comparator_2_eq));  // open: gt, lt

  // Other names for the same wires on the sheet: check = in_2; secclk = in_1; stage[1:0] = in_3
endmodule

module stop (
  output [31:0] out_1,
  output [31:0] out_2
);


  assign out_1 = 32'h7e425a;
  assign out_2 = 32'h5a427e00;
endmodule

module timer (
  input  in_1,
  input  in_2,
  input  [1:0] in_3,
  input  [7:0] in_4,
  output [3:0] out_5,
  output [3:0] out_6,
  output [3:0] out_7,
  output out_8
);

  wire and_1_out, comparator_1_eq, comparator_2_lt, not_1_out, or_1_out, or_2_out;
  wire [7:0] multiplexer_1_out, num, register_2_q, subtractor_1_out;

  Subtractor subtractor_1 (.a(num), .b(8'h1), .out(subtractor_1_out));  // open: bin, bout
  ROM #(.dataWidth(12)) rom_1 (.addr(num), .data({out_5, out_6, out_7}));  // open: sel
  Hex_Digit_Display hex_digit_display_1 (.value(out_5));  // open: dp
  Multiplexer #(.select(2), .width(8)) multiplexer_1 (
    .in0({8{1'b0}}), .in1(in_4), .in2(subtractor_1_out), .in3(subtractor_1_out), .out(multiplexer_1_out),
    .sel(in_3));  // open: en
  Register register_1 (.D(multiplexer_1_out), .Q(num), .clk(in_2), .clr(in_1));  // open: en
  Hex_Digit_Display hex_digit_display_2 (.value(out_6));  // open: dp
  Hex_Digit_Display hex_digit_display_3 (.value(out_7));  // open: dp
  or or_1 (or_1_out, num[7], num[6], num[5], num[4], num[3], num[2], num[1], num[0]);
  Comparator #(.width(2)) comparator_1 (.a(in_3), .b(2'b10), .eq(comparator_1_eq));  // open: gt, lt
  not not_1 (not_1_out, or_1_out);
  Multiplexer multiplexer_2 (.in0(1'b0), .in1(1'b1), .out(out_8), .sel(and_1_out));  // open: en
  and and_1 (and_1_out, comparator_1_eq, or_2_out);
  or or_2 (or_2_out, not_1_out, comparator_2_lt);
  Register register_2 (.D(num), .Q(register_2_q), .clk(in_2));  // open: en, clr
  Comparator comparator_2 (.a(register_2_q), .b(num), .lt(comparator_2_lt));  // open: gt, eq

  // Other names for the same wires on the sheet: max[7:0] = in_4; reset = in_1; secclk = in_2; stage[1:0] = in_3

  // Notes on the sheet:
  //   contents of rom_1 (hex, n*v repeats v):
  //   0 1 2 3 4 5 6 7 8 9 10 11 12 13 14 15 16 17 18 19 20 21 22 23 24 25 26 27 28 29 30 31 32 33 34 35 36
  //   37 38 39 40 41 42 43 44 45 46 47 48 49 50 51 52 53 54 55 56 57 58 59 60 61 62 63 64 65 66 67 68 69
  //   70 71 72 73 74 75 76 77 78 79 80 81 82 83 84 85 86 87 88 89 90 91 92 93 94 95 96 97 98 99 100 101
  //   102 103 104 105 106 107 108 109 110 111 112 113 114 115 116 117 118 119 120 121 122 123 124 125 126
  //   127 128 129 130 131 132 133 134 135 136 137 138 139 140 141 142 143 144 145 146 147 148 149 150 151
  //   152 153 154 155 156 157 158 159 160 161 162 163 164 165 166 167 168 169 170 171 172 173 174 175 176
  //   177 178 179 180 181 182 183 184 185 186 187 188 189 190 191 192 193 194 195 196 197 198 199 200 201
  //   202 203 204 205 206 207 208 209 210 211 212 213 214 215 216 217 218 219 220 221 222 223 224 225 226
  //   227 228 229 230 231 232 233 234 235 236 237 238 239 240 241 242 243 244 245 246 247 248 249 250 251
  //   252 253 254 255
endmodule

module secclock (
  input  in_1,
  input  in_2,
  output out_3
);

  wire [3:0] adder_1_out, ss;

  Adder #(.width(4)) adder_1 (.a(ss), .b(4'b0001), .out(adder_1_out));  // open: cin, cout
  Register #(.width(4)) register_1 (.D(adder_1_out), .Q(ss), .clk(in_1), .clr(in_2));  // open: en
  Multiplexer #(.select(4)) multiplexer_1 (
    .in0(1'b0), .in1(1'b0), .in2(1'b0), .in3(1'b0), .in4(1'b0), .in5(1'b0), .in6(1'b0), .in7(1'b0),
    .in8(1'b0), .in9(1'b0), .in10(1'b0), .in11(1'b0), .in12(1'b0), .in13(1'b0), .in14(1'b0), .in15(1'b1),
    .out(out_3), .sel(ss));  // open: en

  // Other names for the same wires on the sheet: clk = in_1; start = in_2
endmodule

module stage_control (
  input  in_1,
  input  in_2,
  input  in_3,
  input  in_4,
  input  [1:0] in_5,
  input  in_6,
  output [1:0] out_7,
  output out_8
);

  wire and_1_out, and_4_out, comparator_1_eq, comparator_2_eq, comparator_3_eq, comparator_4_eq,
       comparator_5_eq, comparator_6_eq, comparator_7_eq, comparator_8_eq, temp_clk, undriven;
  wire [1:0] adder_3_out, multiplexer_2_out, multiplexer_4_out, ssss;
  wire [3:0] adder_1_out, adder_2_out, ss, sss;
  wire [3:1] and_3_out;

  Adder #(.width(4)) adder_1 (.a(sss), .b(4'b0001), .out(adder_1_out));  // open: cin, cout
  Comparator #(.width(4)) comparator_1 (.a(4'b0000), .b(sss), .eq(comparator_1_eq));  // open: gt, lt
  Adder #(.width(4)) adder_2 (.a(ss), .b(4'b0001), .out(adder_2_out));  // open: cin, cout
  Register #(.width(4)) register_1 (.D(adder_1_out), .Q(sss), .clk(temp_clk), .clr(in_1));  // open: en
  Multiplexer multiplexer_1 (.in0(1'b0), .in1(1'b1), .out(out_8), .sel(and_1_out));  // open: en
  and and_1 (and_1_out, comparator_1_eq, in_1, comparator_2_eq);
  Comparator #(.width(2)) comparator_2 (.a(2'b01), .b(in_5), .eq(comparator_2_eq));  // open: gt, lt
  Register #(.width(4)) register_2 (.D(adder_2_out), .Q(ss), .clk(in_3), .clr(in_1));  // open: en
  Comparator #(.width(2)) comparator_3 (.a(2'b10), .b(in_5), .eq(comparator_3_eq));  // open: gt, lt
  and and_2 (and_3_out[3], comparator_3_eq, in_6);
  Comparator #(.width(4)) comparator_4 (.a(4'b0000), .b(ss), .eq(comparator_4_eq));  // open: gt, lt
  Multiplexer #(.select(4), .width(2)) multiplexer_2 (
    .in0(out_7), .in1(2'b01), .in2(2'b10), .in3(out_7), .in4(2'b00), .in5(out_7), .in6(out_7), .in7(out_7),
    .in8(2'b11), .in9(out_7), .in10(out_7), .in11(out_7), .in12(out_7), .in13(out_7), .in14(out_7),
    .in15(out_7), .out(multiplexer_2_out), .sel({and_3_out[3], in_4, and_3_out[1], in_1}));  // open: en
  Comparator #(.width(4)) comparator_5 (.a(4'b0011), .b(sss), .eq(comparator_5_eq));  // open: gt, lt
  and and_3 (and_3_out[1], comparator_5_eq, comparator_6_eq);
  Comparator #(.width(2)) comparator_6 (.a(2'b01), .b(in_5), .eq(comparator_6_eq));  // open: gt, lt
  Adder #(.width(2)) adder_3 (.a(ssss), .b(2'b01), .out(adder_3_out));  // open: cin, cout
  Multiplexer #(.select(4)) multiplexer_3 (
    .in0(1'b1), .in1(1'b0), .in2(1'b0), .in3(1'b0), .in4(1'b0), .in5(1'b0), .in6(1'b0), .in7(1'b0),
    .in8(1'b0), .in9(1'b0), .in10(1'b0), .in11(1'b0), .in12(1'b0), .in13(1'b0), .in14(1'b0), .in15(1'b0),
    .out(temp_clk), .sel(ss));  // open: en
  Multiplexer #(.width(2)) multiplexer_4 (
    .in0(multiplexer_2_out), .in1(2'b10), .out(multiplexer_4_out), .sel(and_4_out));  // open: en
  and and_4 (and_4_out, comparator_8_eq, comparator_7_eq);
  Comparator #(.width(2)) comparator_7 (.a(2'b11), .b(ssss), .eq(comparator_7_eq));  // open: gt, lt
  Register #(.width(2)) register_3 (.D(adder_3_out), .Q(ssss), .clk(in_3), .clr(in_6));  // open: en
  Comparator #(.width(2)) comparator_8 (.a(2'b11), .b(in_5), .eq(comparator_8_eq));  // open: gt, lt
  Register #(.width(2)) register_4 (.D(multiplexer_4_out), .Q(out_7), .clk(in_3), .clr(undriven));  // open: en

  // Other names for the same wires on the sheet: start = in_1; end = in_4; check = in_6; clk = in_3; reset = out_8;
  //   secclk = in_2; stage[1:0] = in_5
endmodule

module check_key (
  input  [6:0] in_1,
  input  [1:0] in_2,
  output out_3,
  output out_4
);

  wire and_1_out, and_2_out, and_3_out, and_4_out, comparator_1_eq, comparator_2_eq, comparator_3_eq,
       comparator_4_eq, comparator_5_eq, comparator_6_eq, comparator_7_eq, comparator_8_eq, comparator_9_eq,
       or_1_out;

  Comparator #(.width(7)) comparator_1 (.a(in_1), .b({7{1'b0}}), .eq(comparator_1_eq));  // open: gt, lt
  not not_1 (out_3, comparator_1_eq);
  Comparator #(.width(7)) comparator_2 (.a(in_1), .b(7'b1110111), .eq(comparator_2_eq));  // open: gt, lt
  Comparator #(.width(2)) comparator_3 (.a(in_2), .b(2'b00), .eq(comparator_3_eq));  // open: gt, lt
  Comparator #(.width(7)) comparator_4 (.a(in_1), .b(7'b1100100), .eq(comparator_4_eq));  // open: gt, lt
  Comparator #(.width(2)) comparator_5 (.a(in_2), .b(2'b01), .eq(comparator_5_eq));  // open: gt, lt
  Comparator #(.width(7)) comparator_6 (.a(in_1), .b(7'b1110011), .eq(comparator_6_eq));  // open: gt, lt
  Comparator #(.width(2)) comparator_7 (.a(in_2), .b(2'b10), .eq(comparator_7_eq));  // open: gt, lt
  Comparator #(.width(7)) comparator_8 (.a(in_1), .b(7'b1100001), .eq(comparator_8_eq));  // open: gt, lt
  Comparator #(.width(2)) comparator_9 (.a(in_2), .b(2'b11), .eq(comparator_9_eq));  // open: gt, lt
  and and_1 (and_1_out, comparator_2_eq, comparator_3_eq);
  and and_2 (and_2_out, comparator_4_eq, comparator_5_eq);
  and and_3 (and_3_out, comparator_6_eq, comparator_7_eq);
  and and_4 (and_4_out, comparator_8_eq, comparator_9_eq);
  or or_1 (or_1_out, and_1_out, and_2_out, and_3_out, and_4_out);
  and and_5 (out_4, or_1_out, out_3);

  // Other names for the same wires on the sheet: check = out_4; click = out_3; keyboard[6:0] = in_1;
  //   random[1:0] = in_2
endmodule

module score (
  input  in_1,
  input  in_2,
  input  in_3,
  input  in_4,
  input  [1:0] in_5,
  output [3:0] out_6,
  output [3:0] out_7,
  output [3:0] out_8
);

  wire [2:2] comparator_1_lt;
  wire [7:0] adder_1_out, multiplexer_1_out, score, subtractor_1_out;

  Adder adder_1 (.a(score), .b(8'h1), .out(adder_1_out));  // open: cin, cout
  Subtractor subtractor_1 (.a(score), .b(8'h1), .out(subtractor_1_out));  // open: bin, bout
  Comparator comparator_1 (.a(score), .b({8{1'b0}}), .lt(comparator_1_lt[2]));  // open: gt, eq
  ROM #(.dataWidth(12)) rom_1 (.addr(score), .data({out_6, out_7, out_8}));  // open: sel
  Hex_Digit_Display hex_digit_display_1 (.value(out_6));  // open: dp
  Multiplexer #(.select(3), .width(8)) multiplexer_1 (
    .in0(score), .in1(score), .in2(subtractor_1_out), .in3(adder_1_out), .in4({8{1'b0}}), .in5({8{1'b0}}),
    .in6({8{1'b0}}), .in7({8{1'b0}}), .out(multiplexer_1_out), .sel({comparator_1_lt[2], in_4, in_3}));  // open: en
  Hex_Digit_Display hex_digit_display_2 (.value(out_7));  // open: dp
  Register register_1 (.D(multiplexer_1_out), .Q(score), .clk(in_2), .clr(in_1));  // open: en
  Hex_Digit_Display hex_digit_display_3 (.value(out_8));  // open: dp

  // Other names for the same wires on the sheet: check = in_3; click = in_4; clk = in_2; reset = in_1;
  //   stage[1:0] = in_5

  // Notes on the sheet:
  //   contents of rom_1 (hex, n*v repeats v):
  //   0 1 2 3 4 5 6 7 8 9 10 11 12 13 14 15 16 17 18 19 20 21 22 23 24 25 26 27 28 29 30 31 32 33 34 35 36
  //   37 38 39 40 41 42 43 44 45 46 47 48 49 50 51 52 53 54 55 56 57 58 59 60 61 62 63 64 65 66 67 68 69
  //   70 71 72 73 74 75 76 77 78 79 80 81 82 83 84 85 86 87 88 89 90 91 92 93 94 95 96 97 98 99 100 101
  //   102 103 104 105 106 107 108 109 110 111 112 113 114 115 116 117 118 119 120 121 122 123 124 125 126
  //   127 128 129 130 131 132 133 134 135 136 137 138 139 140 141 142 143 144 145 146 147 148 149 150 151
  //   152 153 154 155 156 157 158 159 160 161 162 163 164 165 166 167 168 169 170 171 172 173 174 175 176
  //   177 178 179 180 181 182 183 184 185 186 187 188 189 190 191 192 193 194 195 196 197 198 199 200 201
  //   202 203 204 205 206 207 208 209 210 211 212 213 214 215 216 217 218 219 220 221 222 223 224 225 226
  //   227 228 229 230 231 232 233 234 235 236 237 238 239 240 241 242 243 244 245 246 247 248 249 250 251
  //   252 253 254 255
endmodule

module ready (
  input  in_1,
  input  in_2,
  output [31:0] out_3,
  output [31:0] out_4
);

  wire [1:0] adder_1_out, gg, gg_t;

  Multiplexer #(.select(2), .width(8)) multiplexer_1 (
    .in0(8'h49), .in1({8{1'b0}}), .in2({8{1'b0}}), .in3({8{1'b0}}), .out(out_3[31:24]), .sel(gg));  // open: en
  Multiplexer #(.select(2), .width(8)) multiplexer_2 (
    .in0(8'h49), .in1({8{1'b0}}), .in2({8{1'b0}}), .in3({8{1'b0}}), .out(out_3[23:16]), .sel(gg_t));  // open: en
  Multiplexer #(.select(2), .width(8)) multiplexer_3 (
    .in0(8'h49), .in1(8'h6f), .in2({8{1'b0}}), .in3({8{1'b0}}), .out(out_3[15:8]), .sel(gg_t));  // open: en
  Multiplexer #(.select(2), .width(8)) multiplexer_4 (
    .in0(8'h7f), .in1(8'h49), .in2({8{1'b0}}), .in3({8{1'b0}}), .out(out_3[7:0]), .sel(gg_t));  // open: en
  DotMatrix #(.matrixcols(8), .matrixrows(8)) dotmatrix_1 (
    .col0(out_3[31:24]), .col1(out_3[23:16]), .col2(out_3[15:8]), .col3(out_3[7:0]), .col4(out_4[31:24]),
    .col5(out_4[23:16]), .col6(out_4[15:8]), .col7(out_4[7:0]));
  Multiplexer #(.select(2), .width(8)) multiplexer_5 (
    .in0({8{1'b0}}), .in1(8'h49), .in2({8{1'b0}}), .in3({8{1'b0}}), .out(out_4[31:24]), .sel(gg_t));  // open: en
  Multiplexer #(.select(2), .width(8)) multiplexer_6 (
    .in0({8{1'b0}}), .in1(8'h79), .in2(8'h10), .in3({8{1'b0}}), .out(out_4[23:16]), .sel(gg_t));  // open: en
  Multiplexer #(.select(2), .width(8)) multiplexer_7 (
    .in0({8{1'b0}}), .in1({8{1'b0}}), .in2(8'h20), .in3({8{1'b0}}), .out(out_4[15:8]), .sel(gg_t));  // open: en
  Multiplexer #(.select(2), .width(8)) multiplexer_8 (
    .in0({8{1'b0}}), .in1({8{1'b0}}), .in2(8'h7f), .in3({8{1'b0}}), .out(out_4[7:0]), .sel(gg_t));  // open: en
  Adder #(.width(2)) adder_1 (.a(gg), .b(2'b01), .out(adder_1_out));  // open: cin, cout
  Register #(.width(2)) register_1 (.D(adder_1_out), .Q(gg), .clk(in_1), .clr(in_2));  // open: en

  // Other names for the same wires on the sheet: reset = in_2; secclk = in_1
endmodule

module pass (
  input  in_1,
  output [31:0] out_2,
  output [31:0] out_3
);

  wire [7:0] undriven, undriven_2, undriven_3, undriven_4, undriven_5, undriven_6, undriven_7, undriven_8,
       undriven_9, undriven_10, undriven_11, undriven_12, undriven_13, undriven_14, undriven_15, undriven_16;

  Multiplexer #(.select(2), .width(8)) multiplexer_1 (
    .in0({8{1'b0}}), .in1({8{1'b0}}), .in2(undriven_6), .in3(undriven), .out(out_2[31:24]), .sel({1'b0, in_1}));  // open: en
  Multiplexer #(.select(2), .width(8)) multiplexer_2 (
    .in0(8'h20), .in1({8{1'b0}}), .in2(undriven_2), .in3(undriven_3), .out(out_2[23:16]), .sel({1'b0, in_1}));  // open: en
  Multiplexer #(.select(2), .width(8)) multiplexer_3 (
    .in0(8'h24), .in1(8'h6f), .in2(undriven_7), .in3(undriven_4), .out(out_2[15:8]), .sel({1'b0, in_1}));  // open: en
  Multiplexer #(.select(2), .width(8)) multiplexer_4 (
    .in0(8'h2), .in1(8'h49), .in2(undriven_8), .in3(undriven_5), .out(out_2[7:0]), .sel({1'b0, in_1}));  // open: en
  DotMatrix #(.matrixcols(8), .matrixrows(8)) dotmatrix_1 (
    .col0(out_2[31:24]), .col1(out_2[23:16]), .col2(out_2[15:8]), .col3(out_2[7:0]), .col4(out_3[31:24]),
    .col5(out_3[23:16]), .col6(out_3[15:8]), .col7(out_3[7:0]));
  Multiplexer #(.select(2), .width(8)) multiplexer_5 (
    .in0(8'h2), .in1(8'h49), .in2(undriven_9), .in3(undriven_10), .out(out_3[31:24]), .sel({1'b0, in_1}));  // open: en
  Multiplexer #(.select(2), .width(8)) multiplexer_6 (
    .in0(8'h24), .in1(8'h79), .in2(undriven_11), .in3(undriven_12), .out(out_3[23:16]), .sel({1'b0, in_1}));  // open: en
  Multiplexer #(.select(2), .width(8)) multiplexer_7 (
    .in0(8'h20), .in1({8{1'b0}}), .in2(undriven_13), .in3(undriven_14), .out(out_3[15:8]), .sel({1'b0, in_1}));  // open: en
  Multiplexer #(.select(2), .width(8)) multiplexer_8 (
    .in0({8{1'b0}}), .in1({8{1'b0}}), .in2(undriven_15), .in3(undriven_16), .out(out_3[7:0]),
    .sel({1'b0, in_1}));  // open: en

  // Other names for the same wires on the sheet: check = in_1; ff[0] = in_1
endmodule
